# Fritzing sketch kopplingsschema (saved by Fritzing 0.9.4)

parts:
  Part2 = Arduino Uno (Rev3)
  Part3 = InvenSense MPU6050
  DRV_1 = DRV 8825 Stepper Motor Carrier, High Current [part_number="DRV 8825"]
  M2 = Stepper Motor - Bipolar
  BAT1 = BC9VPC [package=bc9vpc]

nets:
  N1: Part2.A4/SDA, Part3.SCL
  N2: Part2.A5/SCL, Part3.SDA
  N3: Part2.D4, DRV_1.STEP
  N4: Part2.D5_PWM, DRV_1.DIRECTION
  3V3: Part2.3V3, Part3.VCC
  GND: Part2.GND, Part3.GND, DRV_1.GROUND_LOG
  N5: DRV_1.VOLTAGE_ST/_MT, BAT1.V+
  N6: DRV_1.GROUND_ST/_MT, BAT1.V-
  N7: DRV_1.OUT_2B, M2.A
  N8: DRV_1.OUT_2A, M2.C
  N9: DRV_1.OUT_1A, M2.B
  N10: DRV_1.OUT_1B, M2.D
